# Fritzing sketch Automatic-double-doors (saved by Fritzing 0.8.7b)
breadboards: 3

parts:
  Parte1 = Arduino Uno (Rev3)
  LED1 = LED - 5mm [color="Red (633nm)" package="5 mm [THT]"]  # not connected
  LED2 = LED - 5mm [color="Red (633nm)" package="5 mm [THT]"]  # not connected
  M3 = DC Motor
  S2 = Toggle Switch [package=THT]
  M4 = DC Motor
  RELAY-ABRIR-2_2 = Relay T73
  RELAY-ABRIR-2_1 = Relay T73
  RELAY-CERRAR-2_2 = Relay T73
  RELAY-CERRAR-2_1 = Relay T73
  RELAY-CERRAR-1_1 = Relay T73
  RELAY-CERRAR-1_2 = Relay T73
  RELAY-ABRIR-1_1 = Relay T73
  RELAY-ABRIR-1_2 = Relay T73
  S9 = Round Pushbutton
  S10 = Toggle Switch [package=THT]
  S11 = Toggle Switch [package=THT]
  S12 = Toggle Switch [package=THT]
  S13 = Toggle Switch [package=THT]
  S14 = Toggle Switch [package=THT]
  S15 = Toggle Switch [package=THT]
  S16 = Toggle Switch [package=THT]
  S17 = Toggle Switch [package=THT]

nets:
  N1: Parte1.D2, RELAY-ABRIR-1_1.C1, RELAY-ABRIR-1_2.C1
  N2: Parte1.D3_PWM, RELAY-CERRAR-1_1.C1, RELAY-CERRAR-1_2.C1
  N3: Parte1.D4, RELAY-ABRIR-2_2.C1, RELAY-ABRIR-2_1.C1
  N4: Parte1.D5_PWM, RELAY-CERRAR-2_2.C1, RELAY-CERRAR-2_1.C1
  N5: Parte1.GND, S2.COM, RELAY-ABRIR-2_2.C2, RELAY-ABRIR-2_1.C2, RELAY-CERRAR-2_2.C2, RELAY-CERRAR-2_1.C2, RELAY-CERRAR-1_1.C2, RELAY-CERRAR-1_2.C2, RELAY-ABRIR-1_1.C2, RELAY-ABRIR-1_2.C2, S9.leg0, S10.COM, S11.COM, S12.COM, S13.COM, S14.COM, S15.COM, S16.COM, S17.COM
  N6: M3.pin_1, RELAY-CERRAR-1_1.NO, RELAY-ABRIR-1_1.NO
  N7: M3.pin_2, RELAY-CERRAR-1_2.NO, RELAY-ABRIR-1_2.NO
  N8: M4.pin_1, RELAY-ABRIR-2_1.NO, RELAY-CERRAR-2_1.NO
  N9: M4.pin_2, RELAY-ABRIR-2_2.NO, RELAY-CERRAR-2_2.NO

custom parts:
  Relay T73: An T73 Mini PCB Relay
